# Fritzing sketch self_driving_car (saved by Fritzing 0.9.3b)
breadboards: 1

parts:
  Raspberry_Pi1 = Raspberry Pi 2
  IC1 = L293D [package=THT]
  J1 = Basic Servo
  hc-sr1 = hc-sr04
  M1 = DC Motor
  R1 = Resistor [tolerance=±5% resistance=330 package="0805 [SMD]"]
  R2 = Resistor [tolerance=±5% resistance=470 package="0805 [SMD]"]

nets:
  N1: Raspberry_Pi1.GPIO17, J1.pulse
  N2: Raspberry_Pi1.GPIO22, R1.Pin_0, R2.Pin_1
  N3: Raspberry_Pi1.GPIO25, IC1.Enable_1
  N4: Raspberry_Pi1.GPIO24, IC1.In_1
  N5: Raspberry_Pi1.GPIO23, IC1.In_2
  GND: Raspberry_Pi1.GND, IC1.0V, J1.gnd, hc-sr1.GND, R2.Pin_0
  N6: Raspberry_Pi1.GPIO18, hc-sr1.Trig
  VCC: Raspberry_Pi1.5V, IC1.+Vmotor, IC1.+V, J1.vcc, hc-sr1.VCC
  N7: IC1.Out_1_(_Controlled_by_Enable_1_), M1.pin_2
  N8: IC1.Out_2_(_Controlled_by_Enable_1_), M1.pin_1
  N9: hc-sr1.Echo, R1.Pin_1
